# Fritzing sketch ble-light-switch (saved by Fritzing 0.9.1b)
breadboards: 1

parts:
  RF1 = nRF8001 Bluetooth LE Breakout
  LED1 = LED - 5mm [color="Red (633nm)" package="5 mm [THT]"]
  R1 = Resistor [tolerance=±5% resistance=220 package=THT]
  R2 = Resistor [tolerance=±5% resistance=10k package=THT]
  Part1 = Arduino Uno (Rev3)
  S2 = Pushbutton [package="[THT]"]

nets:
  N1: RF1.SCK, Part1.D13/SCK
  N2: RF1.MISO, Part1.D12/MISO
  N3: RF1.MOSI, Part1.D11_PWM/MOSI
  N4: RF1.REQ, Part1.D10_PWM/SS
  N5: RF1.RDY, Part1.D2
  N6: RF1.RST, Part1.D9_PWM
  GND: RF1.GND, LED1.cathode, R2.Pin_0, Part1.GND
  VIN: RF1.VIN, Part1.5V, S2.Pin_3, S2.Pin_4
  N7: LED1.anode, R1.Pin_0
  N8: R1.Pin_1, Part1.D3_PWM
  N9: R2.Pin_1, Part1.D4, S2.Pin_1, S2.Pin_2

custom parts:
  nRF8001 Bluetooth LE Breakout: nRF8001 Breakout Board
